# Fritzing sketch Thermostat-Controller (saved by Fritzing 0.9.3b)
circuit board: 6.70345cm x 2.42303cm
breadboards: 1

parts:
  Q1 = NPN-Transistor [package="TO92 [THT]"]
  J1 = female pin header, 5 pins [form="♀ (female)" part_number="connector to thermostat"]
  J2 = female pin header, 5 pins [form="♀ (female)" part_number="connector to Arduino"]
  DS2Y-5-DC5V = DS2Y-5-DC5V [part_number=DS2Y-5-DC5V]
  F1 = FUSE [package=fuse_5mm]
  R-78Bxx-1 = R-78Bxx [part_number=" R-78Bxx-1.0L"]
  C2 = Electrolytic Capacitor [capacitance=22µF voltage=50V package="100 mil [THT, electrolytic]"]
  C1 = Electrolytic Capacitor [capacitance=22µF voltage=50V package="100 mil [THT, electrolytic]"]
  J3 = female pin header, 3 pins [form="♀ (female)" part_number="connector to DS18B20"]
  D1 = Zener Diode [part_number=1N4732A breakdown_voltage=3.6V package="300 mil [THT]"]
  R3 = Resistor [tolerance=±5% resistance=1k package=THT]
  R2 = Resistor [tolerance=±5% resistance=2.2k package=THT]
  R1 = Resistor [tolerance=±5% resistance=4.7k package=THT]

nets:
  N1: Q1.E, J1.pin4, J2.pin4, R-78Bxx-1.connector0, C2.-, C1.-, J3.pin1, R2.Pin_0
  N2: Q1.B, R3.Pin_1, R2.Pin_1
  N3: Q1.C, DS2Y-5-DC5V.connector4, D1.anode
  N4: J1.pin1, DS2Y-5-DC5V.connector5
  N5: J1.pin2, DS2Y-5-DC5V.connector6
  N6: J1.pin3, DS2Y-5-DC5V.connector7
  N7: J1.pin5, F1.1
  N8: J2.pin1, J3.pin3, R1.Pin_1
  N9: J2.pin2, R3.Pin_0
  N10: J2.pin3, J3.pin2, R1.Pin_0
  N11: J2.pin5, DS2Y-5-DC5V.connector3, R-78Bxx-1.connector2, C1.+, D1.cathode
  N12: F1.2, R-78Bxx-1.connector1, C2.+
