# Fritzing sketch Thermostat-Controller_external_components (saved by Fritzing 0.9.3b)
circuit board: 6.70345cm x 2.42303cm

parts:
  WeMos_D1_Mini1 = WeMos D1 Mini
  DS1 = DS18B20 1-Wire Temperature Sensor [part_number=DS18B20]
  J3 = male pin header, 5 pins [form="♂ (male)"]
  J3_2 = female pin header, 3 pins [form="♀ (female)"]

nets:
  N1: WeMos_D1_Mini1.3V3, J3.pin1
  N2: WeMos_D1_Mini1.5V, J3.pin5
  N3: WeMos_D1_Mini1.D5, J3.pin3
  N4: WeMos_D1_Mini1.D6, J3.pin2
  N5: WeMos_D1_Mini1.G, J3.pin4
  N6: DS1.GND, J3_2.pin3
  N7: DS1.DQ, J3_2.pin2
  N8: DS1.VDD, J3_2.pin1
